# Fritzing sketch blinder_control_v1 (saved by Fritzing 0.9.3b)
breadboards: 1

parts:
  Part2 = Arduino Uno (Rev3)
  IR2 = TSOP312.., 314.. [package=THT]
  S2 = Pushbutton [package="[SMD]"]
  R2 = Resistor [tolerance=±5% resistance=4.7k package=THT]
  Part7 = NRF24L01+ Breakout Board
  C1 = Capacitor Polarized [package=cpol-radial-1000uf-25v]
  C2 = Capacitor Polarized [package=nippon_f80]
  Pololu_A1 = Pololu A4988 [package=SO16]
  S3 = Pushbutton [package="[SMD]"]
  R3 = Resistor [tolerance=±5% resistance=4.7k package=THT]
  Power_plug1 = Power plug [part_number=12v]
  M2 = Stepper Motor - Bipolar
  LED1 = smd LED [color="Red (633nm)" package="0603 [SMD]"]
  LED2 = smd LED [color="Red (633nm)" package="0603 [SMD]"]
  R4 = Resistor [tolerance=±5% resistance=220 package=THT]
  R5 = Resistor [tolerance=±5% resistance=220 package=THT]

nets:
  N1: Part2.D8, LED1.anode
  N2: Part2.D9_PWM, Part7.CE
  N3: Part2.D10_PWM/SS, Part7.CS
  N4: Part2.D11_PWM/MOSI, Part7.MOSI
  N5: Part2.D12/MISO, Part7.MISO
  N6: Part2.D13/SCK, Part7.SCK
  N7: Part2.D2, Pololu_A1.DIR
  N8: Part2.D3_PWM, Pololu_A1.STEP
  N9: Part2.D4, IR2.Data
  N10: Part2.D5_PWM, S2.Pin_1, S2.Pin_2, R2.Pin_0
  N11: Part2.D6_PWM, S3.Pin_1, S3.Pin_2, R3.Pin_0
  N12: Part2.D7, LED2.anode
  3V3: Part2.3V3, Part7.VCC, C1.+
  5V: Part2.5V, IR2.Vs, S2.Pin_3, S2.Pin_4, Pololu_A1.VDD, S3.Pin_3, S3.Pin_4
  GND: Part2.GND, IR2.GND, R2.Pin_1, Part7.GND, C1.-, Pololu_A1.GND#8, R3.Pin_1, R4.Pin_1, R5.Pin_1
  N13: C2.+, Pololu_A1.VMOT, Power_plug1.VCC
  N14: C2.-, Pololu_A1.GND#14, Power_plug1.GND
  N15: Pololu_A1.RESET, Pololu_A1.SLEEP
  N16: Pololu_A1.1B, M2.D
  N17: Pololu_A1.1A, M2.C
  N18: Pololu_A1.2A, M2.B
  N19: Pololu_A1.2B, M2.A
  N20: LED1.cathode, R5.Pin_0
  N21: LED2.cathode, R4.Pin_0
